# Fritzing sketch breadboard (saved by Fritzing 0.8.5b)
circuit board: 8.46667cm x 5.64444cm
breadboards: 1

parts:
  LED1 = LED - 3mm [color="Red (633nm)" package="3 mm [THT]"]
  LED2 = LED - 3mm [color="Red (633nm)" package="3 mm [THT]"]
  LED5 = LED - 3mm [color="Red (633nm)" package="3 mm [THT]"]
  R1 = Resistor [tolerance=±5% resistance=220 package=THT]
  R2 = Resistor [tolerance=±5% resistance=220 package=THT]
  R3 = Resistor [tolerance=±5% resistance=220 package=THT]
  R5 = Resistor [tolerance=±5% resistance=220 package=THT]
  LED3 = LED - 3mm [color="Red (633nm)" package="3 mm [THT]"]
  R4 = Resistor [tolerance=±5% resistance=220 package=THT]
  LED4 = LED - 3mm [color="Red (633nm)" package="3 mm [THT]"]
  J1 = Piezo Speaker
  8x8_LED_Modul_mit_MAX1 = 8x8 LED Modul mit MAX7219 [package=THT]
  Raspberry_Pi_1 = Raspberry Pi 3 [part_number=RPI-3-V1.2]

nets:
  N1: LED1.cathode, Raspberry_Pi_1.GIPO24
  N2: LED1.anode, R1.Pin_0
  N3: LED2.cathode, Raspberry_Pi_1.GIPO23
  N4: LED2.anode, R2.Pin_0
  N5: LED5.cathode, Raspberry_Pi_1.GIPO18
  N6: LED5.anode, R5.Pin_0
  N7: R1.Pin_1, R2.Pin_1, R3.Pin_1, R5.Pin_1, R4.Pin_1, J1.pin1, 8x8_LED_Modul_mit_MAX1.GND_Eingang, Raspberry_Pi_1.GND
  N8: R3.Pin_0, LED3.anode
  N9: LED3.cathode, Raspberry_Pi_1.GIPO22
  N10: R4.Pin_0, LED4.anode
  N11: LED4.cathode, Raspberry_Pi_1.GIPO27
  N12: J1.pin2, Raspberry_Pi_1.GIPO17
  N13: 8x8_LED_Modul_mit_MAX1.VCC_Eingang, Raspberry_Pi_1.5V
  N14: 8x8_LED_Modul_mit_MAX1.DIN_Eingang, Raspberry_Pi_1.GIPO10
  N15: 8x8_LED_Modul_mit_MAX1.CS_Eingang, Raspberry_Pi_1.GIPO8
  N16: 8x8_LED_Modul_mit_MAX1.CLK_Eingang, Raspberry_Pi_1.GIPO11
